# Fritzing sketch PrototipoFisico (saved by Fritzing 0.9.3b)
breadboards: 1

parts:
  U2 = NodeMCU V3.0
  J1 = Basic Servo
  J2 = Piezo Speaker
  J3 = Basic Servo
  J4 = Basic Force Sensing Resistor (FSR) [package=THT]
  R1 = Resistor [tolerance=±5% resistance=10k package=THT]
  J5 = Infrared Proximity Sensor

nets:
  GND: U2.GND, J1.gnd, J2.pin1, J3.gnd
  N1: U2.A0, J4.pin_1, R1.Pin_0
  VCC: J1.vcc, J3.vcc
  N2: J4.pin_0, J5.Vcc
  N3: R1.Pin_1, J5.GND

custom parts:
  NodeMCU V3.0: ESP8266 based NodeMCU
